# Fritzing sketch myBoblight (saved by Fritzing 0.9.3b)
circuit board: 6.47cm x 5.3cm
breadboards: 1

parts:
  Componente1 = Arduino Uno (Rev3)
  LIR = LED - 3mm [color="Orange (620nm)" package="3 mm [THT]"]
  LSat = LED - 3mm [color="Red (633nm)" part_number="Pin 13" package="3 mm [THT]"]
  C1 = Electrolytic Capacitor [capacitance=1mF voltage=16V package="300 mil [THT, electrolytic]"]
  IR1 = TSOP312.., 314.. [package=THT]
  R4 = Resistor [tolerance=±5% resistance=1k package=THT]
  U1 = XBee
  L3 = LED - 3mm [color="Yellow (574nm)" package="3 mm [THT]"]
  L4 = LED - 3mm [color="Green (570nm)" package="3 mm [THT]"]
  R5 = Resistor [tolerance=±5% resistance=1k package=THT]
  R6 = Resistor [tolerance=±5% resistance=1k package=THT]
  J1 = male pin header, 3 pins [form="♂ (male)"]

nets:
  N1: Componente1.D12/MISO, R4.Pin_0
  N2: Componente1.D13/SCK, LIR.anode
  GND: Componente1.GND, LIR.cathode, LSat.cathode, C1.-, IR1.GND, U1.GND, L3.cathode, L4.cathode, J1.pin1
  N3: Componente1.D0/RX, U1.pin2
  N4: Componente1.D1/TX, U1.pin3
  N5: Componente1.D2, IR1.Data
  N6: Componente1.D6_PWM, J1.pin2
  3V3: Componente1.3V3, U1.VCC
  N7: Componente1.5V, C1.+, IR1.Vs, J1.pin3
  N8: LSat.anode, R4.Pin_1
  N9: U1.pin6, R5.Pin_0
  N10: U1.pin15, U1.pin16, R6.Pin_0
  N11: L3.anode, R5.Pin_1
  N12: L4.anode, R6.Pin_1
